# Fritzing sketch DebugBoard (saved by Fritzing 0.8.7b)
breadboards: 1

parts:
  Bauteil1 = Arduino Uno (Rev3)
  R1 = Resistor [tolerance=±5% resistance=1M package=THT]
  C1 = Ceramic Capacitor [capacitance=100nF package="100 mil [THT, multilayer]"]
  U1 = LM 358 Dual Op-Amp [package="DIP8 [THT]"]
  R2 = Resistor [tolerance=±5% resistance=220 package=THT]
  R3 = Resistor [tolerance=±5% resistance=330 package=THT]
  U2 = Voltage Regulator - 5V [part_number=LM317T package="TO220 [THT]"]
  R4 = Resistor [tolerance=±5% resistance=220 package=THT]
  R5 = Resistor [tolerance=±5% resistance=1M package=THT]
  C2 = Ceramic Capacitor [capacitance=100nF package="100 mil [THT, multilayer]"]
  R6 = Resistor [tolerance=±5% resistance=220 package=THT]
  R7 = Resistor [tolerance=±5% resistance=330 package=THT]
  U3 = Voltage Regulator - 5V [part_number=LM317T package="TO220 [THT]"]
  R8 = Resistor [tolerance=±5% resistance=220 package=THT]
  U5 = Voltage Regulator - 5V [package="TO220 [THT]"]
  C5 = Electrolytic Capacitor [capacitance=4.7µF package="100 mil [THT, electrolytic]"]
  C6 = Electrolytic Capacitor [capacitance=4.7µF package="100 mil [THT, electrolytic]"]
  L3 = Inductor [inductance=8.7 current=1.5 package="400 mil [THT]"]
  R14 = Trimmer Potentiometer [maximum_resistance=10kΩ package=THT]
  R15 = Trimmer Potentiometer [maximum_resistance=10kΩ package=THT]
  LM4040CIZ-5_0-NOPB1 = TRANSISTOR_NPN [package=to-92]
  R16 = Resistor [tolerance=±5% resistance=47k package=THT]
  R17 = Resistor [tolerance=±5% resistance=22k package=THT]
  R18 = Resistor [tolerance=±5% resistance=47k package=THT]
  R19 = Resistor [tolerance=±5% resistance=22k package=THT]
  R20 = Resistor [tolerance=±5% resistance=540 package=THT]
  J1 = longpad pin header, 10 pins [form="long pad"]
  J2 = Screw terminal - 2 pins [package=THT]
  LED1 = LED - 5mm [color="Red (633nm)" package="5 mm [THT]"]  # not connected
  J3 = longpad pin header, 2 pins [form="long pad"]
  R21 = Resistor [tolerance=±5% resistance=220 package=THT]  # not connected

nets:
  N1: Bauteil1.A0, R18.Pin_0, R19.Pin_1
  N2: Bauteil1.A1, R16.Pin_0, R17.Pin_1
  N3: Bauteil1.D8, J3.pin2
  GND: Bauteil1.GND, C1.0, U1.connector3, R2.Pin_0, C2.0, R6.Pin_0, U5.GND, C5.-, C6.-, R14.wiper, R15.wiper, LM4040CIZ-5_0-NOPB1.E, J2.pin2
  N4: Bauteil1.AREF, LM4040CIZ-5_0-NOPB1.B, R20.Pin_1
  N5: Bauteil1.D5_PWM, R1.Pin_0
  N6: Bauteil1.D6_PWM, R5.Pin_0
  N7: Bauteil1.D7, J3.pin1
  5V: Bauteil1.5V, U5.output_voltage, R20.Pin_0
  N8: R1.Pin_1, C1.1, U1.connector2
  N9: U1.connector0, R3.Pin_0, U2.GND, R4.Pin_1
  N10: U1.connector1, R2.Pin_1, R4.Pin_0
  N11: U1.connector4, R5.Pin_1, C2.1
  N12: U1.connector5, R6.Pin_1, R8.Pin_0
  N13: U1.connector6, R7.Pin_0, U3.GND, R8.Pin_1
  20V: U1.connector7, U2.input_voltage, U3.input_voltage, C6.+, L3.pin_0, J2.pin1
  N14: R3.Pin_1, U2.output_voltage, R19.Pin_0, J1.pin1
  N15: R7.Pin_1, U3.output_voltage, R17.Pin_0, J1.pin2
  N16: U5.input_voltage, C5.+, L3.pin_1
  N17: R14.leg2, R16.Pin_1
  N18: R15.leg2, R18.Pin_1

notes:
  R4 / R2 und R6 / R8 berechnen
  Spannungsmessung Source 1
  Spannungsmessung Source 2
