# Fritzing sketch ZHSG (saved by Fritzing 0.8.7b)
circuit board: 8.11006cm x 5.34977cm
circuit board: 5cm x 11.2cm
breadboards: 1

parts:
  Arduino = Arduino Uno (Rev3)
  LCD1 = LCD screen
  R2 = Resistor [tolerance=±5% resistance=1.5k package=THT]
  R4 = Resistor [tolerance=±5% resistance=1.5k package=THT]
  R5 = Resistor [tolerance=±5% resistance=540 package=THT]
  R6 = Resistor [tolerance=±5% resistance=22k package=THT]
  R7 = Resistor [tolerance=±5% resistance=47k package=THT]
  R8 = Resistor [tolerance=±5% resistance=22k package=THT]
  R9 = Resistor [tolerance=±5% resistance=47k package=THT]
  R10 = Resistor [tolerance=±5% resistance=1k package=THT]
  R11 = Resistor [tolerance=±5% resistance=1k package=THT]
  Q1 = MOSFET-NCHANNEL [package=to-92]
  R14 = Resistor [tolerance=±5% resistance=100k package=THT]
  R15 = Resistor [tolerance=±5% resistance=220 package=THT]
  R16 = Resistor [tolerance=±5% resistance=100 package=THT]
  R17 = Trimmer Potentiometer [maximum_resistance=10kΩ package=THT]
  J2 = longpad pin header, 2 pins [form="long pad"]
  Q2 = NPN-Transistor [package="TO92 [THT]"]
  R18 = Resistor [tolerance=±5% resistance=4.7k package=THT]
  U4 = Voltage Regulator - 5V [package="TO220 [THT]"]
  C3 = Electrolytic Capacitor [capacitance=4.7µF package="100 mil [THT, electrolytic]"]
  C4 = Electrolytic Capacitor [capacitance=4.7µF package="100 mil [THT, electrolytic]"]
  L2 = Inductor [inductance=8.7 current=1.5 package="400 mil [THT]"]
  U2 = TLP621 [package=THT]
  U1 = TLP621 [package=THT]
  U5 = TLP621 [package=THT]
  R19 = Resistor [tolerance=±5% resistance=1k package=THT]
  R20 = Resistor [tolerance=±5% resistance=1.5k package=THT]
  IN = screw terminal, 8 pins
  R21 = Resistor [tolerance=±5% resistance=100k package=THT]
  J1 = longpad pin header, 8 pins [form="long pad"]
  Out = Screw terminal - 2 pins [package=THT]
  ENCODER1 = Rotary Encoder with Knob
  R22 = Resistor [tolerance=±5% resistance=4.7k package=THT]
  R23 = Resistor [tolerance=±5% resistance=4.7k package=THT]
  C5 = Ceramic Capacitor [capacitance=10nF package="100 mil [THT, multilayer]"]
  C6 = Ceramic Capacitor [capacitance=10nF package="100 mil [THT, multilayer]"]
  R24 = Resistor [tolerance=±5% resistance=82k package=THT]
  R25 = Resistor [tolerance=±5% resistance=82k package=THT]
  R26 = Resistor [tolerance=±5% resistance=10k package=THT]
  J4 = female pin header, 12 pins [form="♀ (female)"]
  J3 = male pin header, 12 pins [form="♂ (male)"]
  LM4040CIZ-5_0-NOPB = TRANSISTOR_NPN [package=to-92-ammo]
  R27 = TRIMPOT [part_number=10k package=3362u-2]
  R28 = TRIMPOT [part_number=10k package=3362u-2]
  F1 = FUSE [package=fuse_5mm]
  F2 = FUSE [package=fuse_5mm]
  F3 = Resettable Fuse PTC [package=ptc]  # not connected

nets:
  N1: Arduino.A0, IN.pin6, J1.pin6
  N2: Arduino.A1, R6.Pin_1, R7.Pin_0
  N3: Arduino.A2, R8.Pin_1, R9.Pin_0
  N4: Arduino.D8, J3.pin10
  N5: Arduino.D9_PWM, Q1.G, R14.Pin_0
  N6: Arduino.D10_PWM/SS, R18.Pin_0
  N7: Arduino.D11_PWM/MOSI, U5.Pin_4, R20.Pin_1
  N8: Arduino.D12/MISO, R4.Pin_1, U2.Pin_4
  N9: Arduino.D13/SCK, R2.Pin_1, U1.Pin_4
  GND: Arduino.GND, LCD1.VSS, LCD1.R/W, LCD1.LED-, R14.Pin_1, R15.Pin_1, R17.leg1, U4.GND, C3.-, C4.-, U2.Pin_2, U2.Pin_3, U1.Pin_2, U1.Pin_3, U5.Pin_2, U5.Pin_3, IN.pin8, R21.Pin_1, J1.pin8, ENCODER1.no_name_yet#3, C5.0, C6.0, R26.Pin_0, J4.pin12, J3.pin12, LM4040CIZ-5_0-NOPB.C, R27.WIPER, R28.WIPER
  N10: Arduino.AREF, R5.Pin_1, LM4040CIZ-5_0-NOPB.B
  N11: Arduino.D0/RX, J3.pin2
  N12: Arduino.D1/TX, J3.pin3
  N13: Arduino.D2, J3.pin4
  N14: Arduino.D3_PWM, J3.pin5
  N15: Arduino.D4, J3.pin6
  N16: Arduino.D5_PWM, J3.pin7
  N17: Arduino.D6_PWM, J3.pin8
  N18: Arduino.D7, J3.pin9
  5V: Arduino.5V, LCD1.VDD, R2.Pin_0, R4.Pin_0, R5.Pin_0, R17.leg2, U4.output_voltage, R20.Pin_0, ENCODER1.no_name_yet#5, R22.Pin_1, R23.Pin_1, J4.pin11, J3.pin11
  N19: LCD1.V0, R17.wiper
  N20: LCD1.RS, J4.pin10
  N21: LCD1.E, J4.pin9
  N22: LCD1.DB4, J4.pin8
  N23: LCD1.DB5, J4.pin7
  N24: LCD1.DB6, J4.pin6
  N25: LCD1.DB7, J4.pin5
  N26: LCD1.LED+, R15.Pin_0, R16.Pin_0
  14V: R6.Pin_0, F2.2
  N27: R7.Pin_1, R28.CCW
  12V: R8.Pin_0, Q1.D, Q2.C, C4.+, L2.pin_0, F1.2
  N28: R9.Pin_1, R27.CCW
  N29: R10.Pin_0, IN.pin5, J1.pin5
  N30: R10.Pin_1, U1.Pin_1
  N31: R11.Pin_0, IN.pin4, J1.pin4
  N32: R11.Pin_1, U2.Pin_1
  N33: Q1.S, J2.pin1, Out.pin1
  N34: R16.Pin_1, J4.pin1
  N35: J2.pin2, Q2.E, R21.Pin_0, Out.pin2
  N36: Q2.B, R18.Pin_1
  N37: U4.input_voltage, C3.+, L2.pin_1
  N38: U5.Pin_1, R19.Pin_1
  N39: R19.Pin_0, IN.pin3, J1.pin3
  N40: IN.pin1, J1.pin1, F1.1
  N41: IN.pin2, J1.pin2, F2.1
  16V: IN.pin7, J1.pin7, J3.pin1
  N42: ENCODER1.no_name_yet#1, R22.Pin_0, R24.Pin_1
  N43: ENCODER1.no_name_yet#2, R23.Pin_0, R25.Pin_1
  N44: ENCODER1.no_name_yet#4, R26.Pin_1, J4.pin4
  N45: C5.1, R24.Pin_0, J4.pin2
  N46: C6.1, R25.Pin_0, J4.pin3

notes:
  Spannungsmessung Batt. 1
  Spannungsmessung Batt. 2
  12 V Zweitbatterie
  GND
  Zündung
  Zuheizer
  12 V Hauptbatterie
  Trennrelais +
  Amaturenbel
  LED 4,5V / 45mA
  Debug Inputs
  Temp Kühlwasser
  Spannungsreferenz
  Vcc
  Pin 8 GND
  Pin 7 Amaturenbeleuchtung
  Pin 6 Temp Kühlwasser
  Pin 5 Kl 15a Zündung
  Pin 4 Zuheizer Uhr
  Pin 3 Steuerung ZH von Board Elek
  Pin 2 12V Hauptbatterie
  Pin 1 12V Zweitbatterie
  Zuheizer +
  +Sek
  +Pri
  xxx
  ZH Uhr
  Kl15a
  Kl58b
  Temp
  Relais+
  ZH

custom parts:
  Rotary Encoder with Knob: Rotary Encoder with 1/4" Shaft and Knob
